# Fritzing sketch AirMonitor (saved by Fritzing 0.9.0b)
circuit board: 8.46667cm x 5.64444cm
breadboards: 1

parts:
  Arduino_Pro_Mini = Arduino Pro Mini v13
  SG1 = Buzzer 12mm [package=buzzer-12mm-ns]  # not connected
  U1 = ENC28J60 [package=ssop28db]  # not connected
  DHT1 = DHT11 Humitidy and Temperature Sensor
  Nokia_5110_LCD_Module1 = Nokia5110LCDModule

nets:
  N1: Arduino_Pro_Mini.D9_PWM, Nokia_5110_LCD_Module1.SCE
  N2: Arduino_Pro_Mini.D8, Nokia_5110_LCD_Module1.RST
  N3: Arduino_Pro_Mini.D7, Nokia_5110_LCD_Module1.D/C
  N4: Arduino_Pro_Mini.D6_PWM, Nokia_5110_LCD_Module1.6_DN_(MOSI)
  N5: Arduino_Pro_Mini.D5_PWM, Nokia_5110_LCD_Module1.SCLK
  N6: Arduino_Pro_Mini.D3_PWM, DHT1.DATA
  VDD: DHT1.VDD, Nokia_5110_LCD_Module1.Vcc
  N7: DHT1.GND, Nokia_5110_LCD_Module1.Grnd

custom parts:
  DHT11 Humitidy and Temperature Sensor: DHT11 Humidity and Temperature Sensor
  : Nokia 5110 LCD with 8 pin. It's a 45mm*45mm module part. Description: The Nokia 5110 is a basic graphic LCD screen for lots of applications. It was originally intended for as a cell phone screen. This one is mounted on an easy to solder PCB. It uses the PCD8544 controller. The PCD8544 is a low power CMOS LCD controller/driver, designed to drive a graphic display of 48 rows and 84 columns. All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
